# Fritzing sketch rpi (saved by Fritzing 0.9.4)

parts:
  S1 = H-Bridge with L298N
  BAT1 = BC9VPC [package=bc9vpc]
  MCU1 = Raspberry Pi Zero
  M1 = DC Motor
  M2 = DC Motor

nets:
  N1: S1.12V, BAT1.V+
  N2: S1.GND, BAT1.V-, MCU1.pin_6, MCU1.pin_9, MCU1.pin_14
  N3: S1.5V, MCU1.pin_2, MCU1.pin_4
  N4: S1.ENA, S1.ENA-5V
  N5: S1.IN1, MCU1.pin_32
  N6: S1.IN2, MCU1.pin_36
  N7: S1.IN3, MCU1.pin_38
  N8: S1.IN4, MCU1.pin_40
  N9: S1.ENB, S1.ENB-5V
  N10: S1.M1-01, M2.pin_2
  N11: S1.M1-02, M2.pin_1
  N12: S1.M2-01, M1.pin_2
  N13: S1.M2-02, M1.pin_1

custom parts:
  H-Bridge with L298N: h-bridge
